// Logisim project alu.circ as structural Verilog: 1 circuit, main circuit alu
module alu (
  input  [31:0] A,
  input  [31:0] B,
  input  [3:0] ALUSel,
  output [31:0] ALUResult
);

  wire [31:0] add0, and7, mul8, mulh9, mulhu11, multiplier_1_out, multiplier_4_out, or6, sll1, slt2, sra13,
       srl5, sub12, subtractor_1_out, xor4;
  wire [63:0] bit_extender_1_out, bit_extender_2_out, bit_extender_4_out, bit_extender_5_out;

  assign bit_extender_1_out = {{32{1'b0}}, A};  // Bit_Extender bit_extender_1
  assign bit_extender_2_out = {{32{1'b0}}, B};  // Bit_Extender bit_extender_2
  Adder #(.width(32)) adder_1 (.a(A), .b(B), .out(add0));  // open: cin, cout
  Shifter #(.width(32)) shifter_1 (.in(A), .\dist (B[4:0]), .out(sll1));
  assign slt2 = {{31{1'b0}}, subtractor_1_out[31]};  // Bit_Extender bit_extender_3
  Subtractor #(.width(32)) subtractor_1 (.a(A), .b(B), .out(subtractor_1_out));  // open: bin, bout
  assign xor4 = A ^ B;  // XOR_Gate xor_1, 32 bits wide
  Shifter #(.shift("lr"), .width(32)) shifter_2 (.in(A), .\dist (B[4:0]), .out(srl5));
  assign or6 = A | B;  // OR_Gate or_1, 32 bits wide
  assign and7 = A & B;  // AND_Gate and_1, 32 bits wide
  Multiplier #(.width(64)) multiplier_1 (
    .a(bit_extender_1_out), .b(bit_extender_2_out), .out({mulhu11, multiplier_1_out}));  // open: cin, cout
  Multiplier #(.mode("twosComplement"), .width(32)) multiplier_2 (.a(A), .b(B), .out(mul8));  // open: cin, cout
  Multiplier #(.width(32)) multiplier_3 (.a(A), .b(B));  // open: out, cin, cout
  Subtractor #(.width(32)) subtractor_2 (.a(A), .b(B), .out(sub12));  // open: bin, bout
  Shifter #(.shift("ar"), .width(32)) shifter_3 (.in(A), .\dist (B[4:0]), .out(sra13));
  assign bit_extender_4_out = {{32{A[31]}}, A};  // Bit_Extender bit_extender_4
  assign bit_extender_5_out = {{32{B[31]}}, B};  // Bit_Extender bit_extender_5
  Multiplier #(.mode("twosComplement"), .width(64)) multiplier_4 (
    .a(bit_extender_4_out), .b(bit_extender_5_out), .out({mulh9, multiplier_4_out}));  // open: cin, cout
  Multiplexer #(.select(4), .width(32)) multiplexer_1 (
    .in0(add0), .in1(sll1), .in2(slt2), .in3({32{1'b0}}), .in4(xor4), .in5(srl5), .in6(or6), .in7(and7),
    .in8(mul8), .in9(mulh9), .in10({32{1'b0}}), .in11(mulhu11), .in12(sub12), .in13(sra13),
    .in14({32{1'b0}}), .in15(B), .out(ALUResult), .sel(ALUSel));

  // Other names for the same wires on the sheet: bsel15[31:0] = B

  // Notes on the sheet:
  //   INPUTS to your circuit
  //   DON'T CHANGE THE LOCATIONS OF THE INPUTS AND OUTPUTS!
  //   OUTPUT from your circuit
endmodule
