// Logisim project control-logic.circ as structural Verilog: 1 circuit, main circuit control_logic
module control_logic (
  input  [31:0] Instruction,
  input  BrEq,
  input  BrLt,
  output PCSel,
  output RegWEn,
  output [2:0] ImmSel,
  output BrUn,
  output ASel,
  output BSel,
  output [3:0] ALUSel,
  output MemWEn,
  output [1:0] WBSel
);

  wire and_1_out, and_2_out, and_3_out, and_4_out, B, f0, f1, f2, f3, f4, f5, f6, f7, fun0, fun1, fun2, I1,
       I2, in0, in1, in2, in3, in4, in5, in6, in7, in8, in9, in10, in11, in12, in13, in14, in15, in16, in17,
       in18, in19, in20, in21, in22, in23, in24, in25, in26, in27, in28, in29, in30, in31, in32, in33, in34,
       in35, not_1_out, not_2_out, opf0, opf1, opf5, opf8, or_2_out, or_3_out, or_4_out, R, S;
  wire [5:0] rominput;
  wire [15:14] rom_1_data;

  ROM #(.addrWidth(6), .dataWidth(16)) rom_1 (
    .addr(rominput), .data({rom_1_data, WBSel, MemWEn, ALUSel, BSel, ASel, BrUn, ImmSel, RegWEn}));
  Comparator #(.width(7)) comparator_1 (.a(Instruction[6:0]), .b(7'b0110011), .eq(R));  // open: gt, lt
  Comparator #(.width(7)) comparator_2 (.a(Instruction[6:0]), .b(7'b0000011), .eq(I1));  // open: gt, lt
  Comparator #(.width(7)) comparator_3 (.a(Instruction[6:0]), .b(7'b0010011), .eq(I2));  // open: gt, lt
  Comparator #(.width(7)) comparator_4 (.a(Instruction[6:0]), .b(7'b0100011), .eq(S));  // open: gt, lt
  Comparator #(.width(7)) comparator_5 (.a(Instruction[6:0]), .b(7'b1100011), .eq(B));  // open: gt, lt
  Comparator #(.width(7)) comparator_6 (.a(Instruction[6:0]), .b(7'b0010111), .eq(in32));  // open: gt, lt
  Comparator #(.width(7)) comparator_7 (.a(Instruction[6:0]), .b(7'b0110111), .eq(in33));  // open: gt, lt
  Comparator #(.width(7)) comparator_8 (.a(Instruction[6:0]), .b(7'b1101111), .eq(in34));  // open: gt, lt
  Comparator #(.width(7)) comparator_9 (.a(Instruction[6:0]), .b(7'b1100111), .eq(in35));  // open: gt, lt
  or or_1 (PCSel, and_1_out, and_2_out, and_3_out, in35, in34, and_4_out);
  Comparator #(.width(3)) comparator_10 (.a(Instruction[14:12]), .b(3'b000), .eq(f0));  // open: gt, lt
  Comparator #(.width(3)) comparator_11 (.a(Instruction[14:12]), .b(3'b001), .eq(f1));  // open: gt, lt
  Comparator #(.width(3)) comparator_12 (.a(Instruction[14:12]), .b(3'b010), .eq(f2));  // open: gt, lt
  Comparator #(.width(3)) comparator_13 (.a(Instruction[14:12]), .b(3'b011), .eq(f3));  // open: gt, lt
  Comparator #(.width(3)) comparator_14 (.a(Instruction[14:12]), .b(3'b100), .eq(f4));  // open: gt, lt
  Comparator #(.width(3)) comparator_15 (.a(Instruction[14:12]), .b(3'b101), .eq(f5));  // open: gt, lt
  Comparator #(.width(3)) comparator_16 (.a(Instruction[14:12]), .b(3'b110), .eq(f6));  // open: gt, lt
  Comparator #(.width(3)) comparator_17 (.a(Instruction[14:12]), .b(3'b111), .eq(f7));  // open: gt, lt
  and and_1 (and_1_out, in27, not_1_out);
  not not_1 (not_1_out, BrEq);
  and and_2 (and_2_out, or_4_out, BrEq);
  and and_3 (and_3_out, or_2_out, BrLt);
  and and_4 (and_4_out, or_3_out, not_2_out);
  not not_2 (not_2_out, BrLt);
  or or_2 (or_2_out, in28, in30);
  or or_3 (or_3_out, in29, in31);
  Comparator #(.width(7)) comparator_18 (.a(Instruction[31:25]), .b({7{1'b0}}), .eq(fun0));  // open: gt, lt
  Comparator #(.width(7)) comparator_19 (.a(Instruction[31:25]), .b(7'b0000001), .eq(fun1));  // open: gt, lt
  Comparator #(.width(7)) comparator_20 (.a(Instruction[31:25]), .b(7'b0100000), .eq(fun2));  // open: gt, lt
  or or_4 (or_4_out, in26, in29, in31);
  and and_5 (opf0, R, f0);
  and and_6 (opf1, R, f1);
  and and_7 (in6, R, f2);
  and and_8 (in5, R, f3);
  and and_9 (in7, R, f4);
  and and_10 (opf5, R, f5);
  and and_11 (in10, R, f6);
  and and_12 (in11, R, f7);
  and and_13 (in12, I1, f0);
  and and_14 (in13, I1, f1);
  and and_15 (in14, I1, f2);
  and and_16 (in15, I2, f0);
  and and_17 (in16, I2, f1);
  and and_18 (in17, I2, f2);
  and and_19 (in18, I2, f4);
  and and_20 (opf8, I2, f5);
  and and_21 (in21, I2, f6);
  and and_22 (in22, I2, f7);
  and and_23 (in23, S, f0);
  and and_24 (in24, S, f1);
  and and_25 (in25, S, f2);
  and and_26 (in26, B, f0);
  and and_27 (in27, B, f1);
  and and_28 (in28, B, f4);
  and and_29 (in29, B, f5);
  and and_30 (in30, B, f6);
  and and_31 (in31, B, f7);
  and and_32 (in0, opf0, fun0);
  and and_33 (in1, opf0, fun1);
  and and_34 (in2, opf0, fun2);
  and and_35 (in3, opf1, fun0);
  and and_36 (in4, opf1, fun1);
  and and_37 (in8, opf5, fun0);
  and and_38 (in9, opf5, fun2);
  and and_39 (in19, opf8, fun0);
  and and_40 (in20, opf8, fun2);
  Priority_Encoder #(.select_enc(6)) priority_encoder_1 (
    .in0(in0), .in1(in1), .in2(in2), .in3(in3), .in4(in4), .in5(in5), .in6(in6), .in7(in7), .in8(in8),
    .in9(in9), .in10(in10), .in11(in11), .in12(in12), .in13(in13), .in14(in14), .in15(in15), .in16(in16),
    .in17(in17), .in18(in18), .in19(in19), .in20(in20), .in21(in21), .in22(in22), .in23(in23), .in24(in24),
    .in25(in25), .in26(in26), .in27(in27), .in28(in28), .in29(in29), .in30(in30), .in31(in31), .in32(in32),
    .in33(in33), .in34(in34), .in35(in35), .out(rominput));  // open: in36, in37, in38, in39, in40, in41, in42, in43, in44, in45, in46, in47, in48, in49, in50, in51, in52, in53, in54, in55, in56, in57, in58, in59, in60, in61, in62, in63, gs, en_out, en_in

  // Other names for the same wires on the sheet: opcode[6:0] = Instruction[6:0]; func3[2:0] = Instruction[14:12];
  //   func7[6:0] = Instruction[31:25]

  // Notes on the sheet:
  //   INPUTS to your circuit
  //   Connect ROM Input here ->
  //   contents of rom_1 (hex, n*v repeats v):
  //   1001 1401 1601 1081 1481 1581 1101 1201 1281 1681 1301 1381 41 41 41 1041 10c1 1141 1241 12c1 16c1
  //   1341 13c1 842 842 842 4*64 74 74 1067 17c7 2069 2041
  //   ROM FOR CONTROL LOGIC
  //   DON'T CHANGE THE LOCATIONS OF THE INPUTS AND OUTPUTS!
  //   This is only if you choose to do the ROM option
  //   CONNECT
  //   WIRE
  //   TO
  //   USE
  //   ROM
  //   OUTPUT from your circuit
  //   Reminder: If using ROM, use combinational logic for PCSel
endmodule
