// Logisim project partial-store.circ as structural Verilog: 1 circuit, main circuit partial_store
module partial_store (
  input  [31:0] Instruction,
  input  [31:0] MemAddress,
  input  [31:0] DataFromReg,
  input  MemWEn,
  output [3:0] MemWriteMask,
  output [31:0] DataToMem
);

  wire and0, and1, and2, and_4_out, and_5_out, and_6_out, and_7_out, and_8_out, and_9_out, and_10_out,
       comparator_5_eq, comparator_6_eq, comparator_7_eq, comparator_8_eq, fu0, fu1, fu2, not_1_out, op;
  wire [1:0] sel;
  wire [4:0] btm2, multiplier_1_out;
  wire [31:0] bit_extender_2_out, bit_extender_3_out, multiplexer_1_out, shifter_1_out;

  Comparator #(.width(7)) comparator_1 (.a(Instruction[6:0]), .b(7'b0100011), .eq(op));  // open: gt, lt
  Comparator #(.width(3)) comparator_2 (.a(Instruction[14:12]), .b(3'b000), .eq(fu0));  // open: gt, lt
  Comparator #(.width(3)) comparator_3 (.a(Instruction[14:12]), .b(3'b001), .eq(fu1));  // open: gt, lt
  Comparator #(.width(3)) comparator_4 (.a(Instruction[14:12]), .b(3'b010), .eq(fu2));  // open: gt, lt
  assign btm2 = {{3{1'b0}}, MemAddress[1:0]};  // Bit_Extender bit_extender_1
  assign bit_extender_2_out = {{24{1'b0}}, DataFromReg[7:0]};  // Bit_Extender bit_extender_2
  assign bit_extender_3_out = {{16{1'b0}}, DataFromReg[15:0]};  // Bit_Extender bit_extender_3
  and and_1 (and0, op, fu0);
  and and_2 (and1, op, fu1);
  and and_3 (and2, op, fu2);
  Multiplexer #(.select(2), .width(32)) multiplexer_1 (
    .in0(bit_extender_2_out), .in1(bit_extender_3_out), .in2(DataFromReg), .out(multiplexer_1_out), .sel(sel));  // open: in3
  Priority_Encoder #(.select_enc(2)) priority_encoder_1 (
    .in0(and0), .in1(and1), .in2(and2), .out(sel));  // open: in3, gs, en_out, en_in
  Multiplier #(.width(5)) multiplier_1 (.a(btm2), .b(5'b01000), .out(multiplier_1_out));  // open: cin, cout
  Shifter #(.width(32)) shifter_1 (.in(multiplexer_1_out), .\dist (multiplier_1_out), .out(shifter_1_out));
  Multiplexer #(.width(32)) multiplexer_2 (.in0({32{1'b0}}), .in1(shifter_1_out), .out(DataToMem), .sel(MemWEn));
  Comparator #(.width(5)) comparator_5 (.a(btm2), .b({5{1'b0}}), .eq(comparator_5_eq));  // open: gt, lt
  Comparator #(.width(5)) comparator_6 (.a(btm2), .b(5'b00001), .eq(comparator_6_eq));  // open: gt, lt
  Comparator #(.width(5)) comparator_7 (.a(btm2), .b(5'b00010), .eq(comparator_7_eq));  // open: gt, lt
  Comparator #(.width(5)) comparator_8 (.a(btm2), .b(5'b00011), .eq(comparator_8_eq));  // open: gt, lt
  and and_4 (and_4_out, comparator_5_eq, MemWEn, and0);
  and and_5 (and_5_out, comparator_5_eq, MemWEn, and1);
  and and_6 (and_6_out, comparator_6_eq, MemWEn, and0);
  and and_7 (and_7_out, comparator_7_eq, MemWEn, and0);
  and and_8 (and_8_out, comparator_7_eq, MemWEn, and1);
  and and_9 (and_9_out, comparator_8_eq, MemWEn, and0);
  and and_10 (and_10_out, MemWEn, and2);
  not not_1 (not_1_out, MemWEn);
  Priority_Encoder #(.select_enc(4)) priority_encoder_2 (
    .in0(not_1_out), .in1(and_4_out), .in2(and_6_out), .in3(and_5_out), .in4(and_7_out), .in8(and_9_out),
    .in12(and_8_out), .in15(and_10_out), .out(MemWriteMask));  // open: in5, in6, in7, in9, in10, in11, in13, in14, gs, en_out, en_in

  // Other names for the same wires on the sheet: opcode[6:0] = Instruction[6:0]; funct3[2:0] = Instruction[14:12]

  // Notes on the sheet:
  //   INPUTS to your circuit
  //   DON'T CHANGE THE LOCATIONS OF THE INPUTS AND OUTPUTS!
  //   OUTPUT from your circuit
endmodule
